# Fritzing sketch no-hell-lights-wemos-pcb (saved by Fritzing 0.9.3b)
circuit board: 5cm x 5cm
breadboards: 1

parts:
  5v = Pad [width=3.25 height=2 connect=center]
  D4 = Pad [width=3.25 height=2 connect=center]
  GND = Pad [width=3.25 height=2 connect=center]
  WeMos_D1_Mini1 = WeMos D1 Mini
  part = female pin header, 1 pin [form="♀ (female)"]
  part_2 = female pin header, 1 pin [form="♀ (female)"]
  I2C = screw terminal, 4 pins
  5k = Resistor [tolerance=±5% resistance=1k package=THT]
  5k_2 = Resistor [tolerance=±5% resistance=1k package=THT]
  D3 = Pad [width=3.25 height=2 connect=center]
  Anal = screw terminal, 4 pins

nets:
  N1: 5v.pad, WeMos_D1_Mini1.5V, part.pin1, Anal.pin3
  N2: D4.pad, 5k.Pin_1
  N3: GND.pad, WeMos_D1_Mini1.G, part_2.pin1, I2C.pin1, Anal.pin4
  N4: WeMos_D1_Mini1.3V3, I2C.pin2
  N5: WeMos_D1_Mini1.A0, Anal.pin1
  N6: WeMos_D1_Mini1.D1, I2C.pin4
  N7: WeMos_D1_Mini1.D2, I2C.pin3
  N8: WeMos_D1_Mini1.D3, 5k_2.Pin_0
  N9: WeMos_D1_Mini1.D4, 5k.Pin_0
  N10: WeMos_D1_Mini1.D5, Anal.pin2
  N11: 5k_2.Pin_1, D3.pad

notes:
  SainSmart 16 relays 5v
  Node MCU (3.3v)
  5v
  3.3v

custom parts:
  WeMos D1 Mini: The D1 mini is a mini wifi board based on ESP-8266EX.
